# Fritzing sketch basic_node (saved by Fritzing 0.9.4)
perfboards: 1

parts:
  U1 = Arduino Uno (Rev3)
  J1 = Camdenboss CTB0158-3 [part_number=KF301-3P package=THT]
  J2 = Camdenboss CTB0158-3 [part_number=KF301-3P package=THT]
  R1 = TRIMPOT [package=trim_pot_pth]
  R2 = TRIMPOT [package=trim_pot_pth]
  R3 = TRIMPOT [package=trim_pot_pth]
  J3 = Camdenboss CTB0158-3 [part_number=KF301-3P package=THT]
  J4 = Camdenboss CTB0158-3 [part_number=KF301-3P package=THT]
  R4 = Resistor [tolerance=±5% resistance=220 package=THT]
  S1 = Pushbutton [package="[THT]"]
  J5 = Camdenboss CTB0158-2 [part_number=KF301-5.0-2 package=THT]  # not connected

nets:
  N1: U1.A0, R1.CW
  N2: U1.A1, R2.CW
  N3: U1.A2, R3.CW
  N4: U1.A4/SDA, J2.pin2
  N5: U1.A5/SCL, J1.pin2
  VPOT: U1.D2, R1.CCW, R2.CCW, R3.CCW
  N6: U1.D3_PWM, J4.pin2
  N7: U1.D5_PWM, J3.pin2
  N8: U1.RESET, S1.Pin_1, S1.Pin_2
  GND: J1.pin1, J2.pin1, J3.pin3, J4.pin3, R4.Pin_0
  5V: J1.pin3, J2.pin3, J3.pin1, J4.pin1
  N9: R4.Pin_1, S1.Pin_3, S1.Pin_4
